# Fritzing sketch BrokerBot_diagram (saved by Fritzing 0.9.3b)
breadboards: 1

parts:
  WeMos_D1_R1 = WeMos D1 R2
  LCD1 = LCD screen
  R3 = Trimmer Potentiometer [maximum_resistance=10kΩ package=THT]
  R4 = Resistor [tolerance=±5% resistance=220 package="2010 [SMD]"]
  ENCODER1 = Rotary Encoder with switch (KY-040) [part_number=KY-040]

nets:
  N1: WeMos_D1_R1.D2, LCD1.DB7
  N2: WeMos_D1_R1.D3, ENCODER1.DT
  N3: WeMos_D1_R1.(D5), LCD1.DB6
  N4: WeMos_D1_R1.(D6), LCD1.DB5
  N5: WeMos_D1_R1.(D7), LCD1.DB4
  N6: WeMos_D1_R1.D8, LCD1.E
  N7: WeMos_D1_R1.D9, LCD1.RS
  GND: WeMos_D1_R1.GND, LCD1.VSS, LCD1.R/W, R3.leg1, R4.Pin_0
  5V: WeMos_D1_R1.5V, LCD1.VDD, LCD1.LED+, R3.leg2
  N8: LCD1.V0, R3.wiper
  N9: LCD1.LED-, R4.Pin_1

custom parts:
  WeMos D1 R2: The D1 R2 is a mini wifi board based on the ESP-8266EX.
  Rotary Encoder with switch (KY-040): A Rotary Encoder with switch
